# Fritzing sketch fade_pwm (saved by Fritzing 1.0.3b)
breadboards: 1

parts:
  Part1 = node32s
  R1 = Resistor [tolerance=±5% resistance=220 package="0402 [SMD]"]
  LED1 = smd LED [color="Red (633nm)" package="0603 [SMD]"]

nets:
  N1: Part1.GND, R1.Pin_0
  N2: Part1.IO16, LED1.anode
  N3: R1.Pin_1, LED1.cathode

notes:
  220Ω Resistor
  Short Leg LED (–) Cathode
