# Fritzing sketch rgb_led (saved by Fritzing 1.0.6)
breadboards: 1

parts:
  Part1 = node32s
  LED6 = RGB LED (com. cathode, rgb) [color="Red (633nm)" current=0.030A package="5 mm [THT]"]  # not connected
  LED7 = RGB LED (com. cathode, rgb) [color="Red (633nm)" current=0.030A package="5 mm [THT]"]
  R2 = Resistor [tolerance=±5% power=0.25W resistance=220 package=THT]
  R3 = Resistor [tolerance=±5% power=0.25W resistance=220 package=THT]
  R4 = Resistor [tolerance=±5% power=0.25W resistance=220 package=THT]

nets:
  N1: Part1.GND, LED7.common_cathode
  N2: Part1.IO5, R4.Pin_0
  N3: Part1.IO17, R3.Pin_0
  N4: Part1.IO16, R2.Pin_0
  N5: LED7.red_anode, R2.Pin_1
  N6: LED7.green_anode, R3.Pin_1
  N7: LED7.blue_anode, R4.Pin_1

notes:
  RGB LED
  flat side
  - red
  - ground (longest)
  - green
  - blue
