# Fritzing sketch pushbutton (saved by Fritzing 1.0.6)
breadboards: 1

parts:
  Part1 = node32s
  R1 = Resistor [tolerance=±5% power=0.25W resistance=220 package=THT]
  S7 = Round Pushbutton
  LED1 = LED - 3mm [color="Red (633nm)" current=0.030A package="3 mm [THT]"]

nets:
  N1: Part1.GND, R1.Pin_0, S7.leg0
  N2: Part1.IO5, S7.leg1
  N3: Part1.IO16, LED1.anode
  N4: R1.Pin_1, LED1.cathode

notes:
  10kΩ Resistors for buttons
  Or use Internal Pullup
  Not pressed = HIGH 3.3V
  Pressed = LOW GND
