# Fritzing sketch shift_register (saved by Fritzing 1.0.6)
breadboards: 1

parts:
  Part1 = node32s
  LED1 = LED - 3mm [color="Red (660nm)" current=0.030A package="3 mm [THT]"]
  R1 = Resistor [tolerance=±5% resistance=220 package="2512 [SMD]"]
  LED2 = LED - 3mm [color="Orange (612nm)" current=0.030A package="3 mm [THT]"]
  R2 = Resistor [tolerance=±5% resistance=220 package="2512 [SMD]"]
  LED3 = LED - 3mm [color="Red (633nm)" current=0.030A package="3 mm [THT]"]
  R3 = Resistor [tolerance=±5% resistance=220 package="2512 [SMD]"]
  LED4 = LED - 3mm [color="Yellow (585nm)" current=0.030A package="3 mm [THT]"]
  R4 = Resistor [tolerance=±5% resistance=220 package="2512 [SMD]"]
  LED5 = LED - 3mm [color="Blue (505nm)" current=0.030A package="3 mm [THT]"]
  R5 = Resistor [tolerance=±5% resistance=220 package="2512 [SMD]"]
  LED6 = LED - 3mm [color="Red (633nm)" current=0.030A package="3 mm [THT]"]
  R6 = Resistor [tolerance=±5% resistance=220 package="2512 [SMD]"]
  LED7 = LED - 3mm [color="Blue (430nm)" current=0.030A package="3 mm [THT]"]
  R7 = Resistor [tolerance=±5% resistance=220 package="2512 [SMD]"]
  LED8 = LED - 3mm [color="Green (555nm)" current=0.030A package="3 mm [THT]"]
  R8 = Resistor [tolerance=±5% resistance=220 package="2512 [SMD]"]
  U1 = 74HC595 [package="DIP16 [THT]"]

nets:
  3.3V: Part1.3.3V, U1.MR, U1.OE, U1.VCC
  GND: Part1.GND, LED1.cathode, LED2.cathode, LED3.cathode, LED4.cathode, LED5.cathode, LED6.cathode, LED7.cathode, LED8.cathode, U1.GND
  N1: Part1.IO23, U1.SH_CP
  N2: Part1.IO22, U1.ST_CP
  N3: Part1.IO21, U1.DS
  N4: LED1.anode, R1.Pin_0
  N5: R1.Pin_1, U1.Q7
  N6: LED2.anode, R2.Pin_0
  N7: R2.Pin_1, U1.Q6
  N8: LED3.anode, R3.Pin_0
  N9: R3.Pin_1, U1.Q5
  N10: LED4.anode, R4.Pin_0
  N11: R4.Pin_1, U1.Q4
  N12: LED5.anode, R5.Pin_0
  N13: R5.Pin_1, U1.Q3
  N14: LED6.anode, R6.Pin_0
  N15: R6.Pin_1, U1.Q2
  N16: LED7.anode, R7.Pin_0
  N17: R7.Pin_1, U1.Q1
  N18: LED8.anode, R8.Pin_0
  N19: R8.Pin_1, U1.Q0
