# Fritzing sketch 7-seg_display (saved by Fritzing 1.0.6)
breadboards: 1

parts:
  Part1 = node32s
  R1 = Resistor [tolerance=±5% resistance=220 package="2512 [SMD]"]
  R2 = Resistor [tolerance=±5% resistance=220 package="2512 [SMD]"]
  R3 = Resistor [tolerance=±5% resistance=220 package="2512 [SMD]"]
  R4 = Resistor [tolerance=±5% resistance=220 package="2512 [SMD]"]
  R5 = Resistor [tolerance=±5% resistance=220 package="2512 [SMD]"]
  R6 = Resistor [tolerance=±5% resistance=220 package="2512 [SMD]"]
  R7 = Resistor [tolerance=±5% resistance=220 package="2512 [SMD]"]
  R8 = Resistor [tolerance=±5% resistance=220 package="2512 [SMD]"]
  U1 = 74HC595 [package="DIP16 [THT]"]
  DI1 = 7-Segment LED Display [package=THT]

nets:
  3.3V: Part1.3.3V, U1.MR, U1.VCC, DI1.commAnode#7
  GND: Part1.GND, U1.GND, U1.OE
  N1: Part1.IO23, U1.SH_CP
  N2: Part1.IO22, U1.ST_CP
  N3: Part1.IO21, U1.DS
  N4: R1.Pin_0, DI1.cathodeA
  N5: R1.Pin_1, U1.Q7
  N6: R2.Pin_0, DI1.cathodeB
  N7: R2.Pin_1, U1.Q6
  N8: R3.Pin_0, DI1.cathodeC
  N9: R3.Pin_1, U1.Q5
  N10: R4.Pin_0, DI1.cathodeD
  N11: R4.Pin_1, U1.Q4
  N12: R5.Pin_0, DI1.cathodeE
  N13: R5.Pin_1, U1.Q3
  N14: R6.Pin_0, DI1.cathodeG
  N15: R6.Pin_1, U1.Q2
  N16: R7.Pin_0, DI1.cathodeF
  N17: R7.Pin_1, U1.Q1
  N18: R8.Pin_0, DI1.cathodeDP
  N19: R8.Pin_1, U1.Q0

notes:
  You must reverse 'g' and 'f' pins on our displays (blue and green wires)
