# Fritzing sketch LCD_display (saved by Fritzing 1.0.6)
breadboards: 1

parts:
  Part1 = node32s
  Part2 = LCD1602-I2C

nets:
  5V: Part1.5V, Part2.VCC
  GND: Part1.GND, Part2.GND
  N1: Part1.IO22, Part2.SCL
  N2: Part1.IO21, Part2.SDA

custom parts:
  LCD1602-I2C: A standard character display, usually with 2x16 characters. Comes in many colors with LCM1602 IIC attached.
