# Fritzing sketch fruit_piano (saved by Fritzing 1.0.6)
breadboards: 1

parts:
  Part1 = node32s
  SG1 = Buzzer 12mm [part_number="– Buzzer +" package=buzzer-12mm-ns]
  S8050 = NPN-Transistor [package="TO92 [THT]"]
  R1 = Resistor [tolerance=±5% power=0.25W resistance=1k package=THT]

nets:
  N1: Part1.IO25, R1.Pin_0
  N2: Part1.5V, SG1.1
  N3: Part1.GND, S8050.E
  N4: S8050.B, R1.Pin_1

notes:
  C5 B4 A4 G4 F4 E4
  C4 D4

custom parts:
  Buzzer 12mm: Buzzer 12mm Spark Fun Electronics SKU : Comp-Buzzer Through hole This is a small 12mm round speaker that operates around the audible 2kHz range. You can use these speakers to create simple music or user interfaces. This is not a true piezoelectric speaker but behaves similarly. Instead of a piezoelectric crystal that vibrates with an electric current, this tiny speaker uses an electromagnet to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
