# Fritzing sketch motor (saved by Fritzing 1.0.6)
breadboards: 1

parts:
  Part1 = node32s
  M1 = DC Motor [voltage_(max)=6V voltage_(min)=3V]
  IC1 = L293D [package=THT]
  VCC1 = Battery block 9V [internal_resistance=0.1Ω]
  part = Ceramic Capacitor [capacitance=0.1µF voltage=35V package="0603 [SMD, multilayer]"]
  part_2 = Ceramic Capacitor [capacitance=0.1µF voltage=35V package="0603 [SMD, multilayer]"]

nets:
  N1: Part1.IO14, IC1.In_2
  N2: Part1.IO12, IC1.Enable_1
  N3: Part1.V_BATT, IC1.0V, VCC1.-, part_2.1
  N4: Part1.IO13, IC1.In_1
  N5: Part1.5V, IC1.+V, part.1
  N6: M1.pin_1, IC1.Out_2_(_Controlled_by_Enable_1_)
  N7: M1.pin_2, IC1.Out_1_(_Controlled_by_Enable_1_)
  N8: IC1.+Vmotor, VCC1.+, part_2.0
